# Fritzing sketch Ultraschallsensor_LCD (saved by Fritzing 0.9.3b)
breadboards: 1

parts:
  Bauteil1 = Arduino Mega 2560 (Rev3)
  hc-sr1 = hc-sr04
  LCD1 = LCD screen
  R1 = Rotary Potentiometer (Small) [maximum_resistance=100kΩ package=THT]

nets:
  N1: Bauteil1.D10_PWM, hc-sr1.Echo
  N2: Bauteil1.D9_PWM, hc-sr1.Trig
  5V: Bauteil1.5V, hc-sr1.VCC, LCD1.VDD, LCD1.LED+, R1.leg1
  GND: Bauteil1.GND, hc-sr1.GND, LCD1.VSS, LCD1.R/W, LCD1.LED-, R1.leg2
  N3: Bauteil1.D1_TX0, LCD1.RS
  N4: Bauteil1.D2_PWM, LCD1.E
  N5: Bauteil1.D4_PWM, LCD1.DB4
  N6: Bauteil1.D5_PWM, LCD1.DB5
  N7: Bauteil1.D6_PWM, LCD1.DB6
  N8: Bauteil1.D7_PWM, LCD1.DB7
  N9: LCD1.V0, R1.wiper
