# Fritzing sketch Ultraschallsensor_LCD_mit_LEDs (saved by Fritzing 0.9.3b)
breadboards: 1

parts:
  Bauteil1 = Arduino Mega 2560 (Rev3)
  hc-sr1 = hc-sr04
  LCD1 = LCD screen
  R1 = Rotary Potentiometer (Small) [maximum_resistance=100kΩ package=THT]
  LED1 = LED - 5mm [color="Green (560nm)" package="5 mm [THT]"]
  R2 = Resistor [tolerance=±5% resistance=100 package=THT]
  LED2 = LED - 5mm [color="Yellow (595nm)" package="5 mm [THT]"]
  R3 = Resistor [tolerance=±5% resistance=100 package=THT]
  LED3 = LED - 5mm [color="Red (633nm)" package="5 mm [THT]"]
  R4 = Resistor [tolerance=±5% resistance=100 package=THT]

nets:
  N1: Bauteil1.D13_PWM, R4.Pin_1
  N2: Bauteil1.D12_PWM, R3.Pin_1
  N3: Bauteil1.D11_PWM, R2.Pin_1
  N4: Bauteil1.D10_PWM, hc-sr1.Echo
  N5: Bauteil1.D9_PWM, hc-sr1.Trig
  5V: Bauteil1.5V, hc-sr1.VCC, LCD1.VDD, LCD1.LED+, R1.leg1
  GND: Bauteil1.GND, hc-sr1.GND, LCD1.VSS, LCD1.R/W, LCD1.LED-, R1.leg2, LED1.cathode, LED2.cathode, LED3.cathode
  N6: Bauteil1.D1_TX0, LCD1.RS
  N7: Bauteil1.D2_PWM, LCD1.E
  N8: Bauteil1.D4_PWM, LCD1.DB4
  N9: Bauteil1.D5_PWM, LCD1.DB5
  N10: Bauteil1.D6_PWM, LCD1.DB6
  N11: Bauteil1.D7_PWM, LCD1.DB7
  N12: LCD1.V0, R1.wiper
  N13: LED1.anode, R2.Pin_0
  N14: LED2.anode, R3.Pin_0
  N15: LED3.anode, R4.Pin_0
